// Logisim project addition.circ as structural Verilog: 1 circuit, main circuit main
module main (
  input  in_1,
  input  in_2,
  input  in_3,
  input  in_4,
  input  in_5,
  input  in_6,
  input  in_7,
  input  in_8,
  input  in_9,
  input  in_10,
  input  in_11,
  input  in_12,
  output out_13,
  output out_14,
  output out_15,
  output out_16,
  output out_17,
  output out_18,
  output out_19
);

  wire and_1_out, and_2_out, and_3_out, and_4_out, and_5_out, and_6_out, and_7_out, and_8_out, and_9_out,
       and_10_out, and_11_out, and_12_out, or_1_out, or_2_out, or_3_out, or_4_out, or_5_out, xor_1_out,
       xor_2_out, xor_3_out, xor_4_out, xor_5_out, xor_6_out;

  xor xor_1 (xor_1_out, in_6, in_12);
  and and_1 (and_1_out, in_6, in_12);
  xor xor_2 (xor_2_out, in_5, in_11);
  and and_2 (and_2_out, in_5, in_11);
  xor xor_3 (xor_3_out, in_4, in_10);
  and and_3 (and_3_out, in_4, in_10);
  xor xor_4 (xor_4_out, in_3, in_9);
  and and_4 (and_4_out, in_3, in_9);
  xor xor_5 (xor_5_out, in_2, in_8);
  and and_5 (and_5_out, in_2, in_8);
  xor xor_6 (xor_6_out, in_1, in_7);
  and and_6 (and_6_out, in_1, in_7);
  xor xor_7 (out_19, 1'b0, xor_1_out);
  and and_7 (and_7_out, 1'b0, xor_1_out);
  xor xor_8 (out_18, or_1_out, xor_2_out);
  and and_8 (and_8_out, or_1_out, xor_2_out);
  xor xor_9 (out_17, or_2_out, xor_3_out);
  and and_9 (and_9_out, or_2_out, xor_3_out);
  xor xor_10 (out_16, or_3_out, xor_4_out);
  and and_10 (and_10_out, or_3_out, xor_4_out);
  xor xor_11 (out_15, or_4_out, xor_5_out);
  and and_11 (and_11_out, or_4_out, xor_5_out);
  xor xor_12 (out_14, or_5_out, xor_6_out);
  and and_12 (and_12_out, or_5_out, xor_6_out);
  or or_1 (or_1_out, and_7_out, and_1_out);
  or or_2 (or_2_out, and_8_out, and_2_out);
  or or_3 (or_3_out, and_9_out, and_3_out);
  or or_4 (or_4_out, and_10_out, and_4_out);
  or or_5 (or_5_out, and_11_out, and_5_out);
  or or_6 (out_13, and_12_out, and_6_out);
endmodule
