// Logisim project counter.circ as structural Verilog: 1 circuit, main circuit main
module main (
  input  in_1,
  input  in_2,
  input  in_3,
  input  in_4,
  input  in_5,
  input  in_6
);

  wire and_1_out, and_2_out, and_3_out, and_4_out, and_5_out, and_6_out, button_1_out, xor_1_out, xor_2_out,
       xor_3_out, xor_4_out, xor_5_out, xor_6_out;

  xor xor_1 (xor_1_out, in_1, and_3_out);
  and and_1 (and_1_out, in_1, and_3_out);
  Button button_1 (.out(button_1_out));
  xor xor_2 (xor_2_out, in_3, and_5_out);
  and and_2 (and_2_out, in_3, and_5_out);
  xor xor_3 (xor_3_out, in_2, and_2_out);
  and and_3 (and_3_out, in_2, and_2_out);
  xor xor_4 (xor_4_out, in_5, and_6_out);
  and and_4 (and_4_out, in_5, and_6_out);
  xor xor_5 (xor_5_out, in_4, and_4_out);
  and and_5 (and_5_out, in_4, and_4_out);
  xor xor_6 (xor_6_out, in_6, button_1_out);
  and and_6 (and_6_out, in_6, button_1_out);
  LED led_1 (.in(and_1_out));
  LED led_2 (.in(xor_1_out));
  LED led_3 (.in(xor_5_out));
  LED led_4 (.in(xor_2_out));
  LED led_5 (.in(xor_3_out));
  LED led_6 (.in(xor_4_out));
  LED led_7 (.in(xor_6_out));
endmodule
