// Logisim project division.circ as structural Verilog: 1 circuit, main circuit main
module main (
  input  in_1,
  input  in_2,
  input  in_3,
  input  in_4,
  input  in_5,
  input  in_6,
  input  in_7,
  input  in_8,
  input  in_9,
  input  in_10,
  input  in_11,
  input  in_12,
  input  in_13,
  input  in_14,
  input  in_15
);

  wire and_1_out, and_2_out, and_3_out, and_4_out, and_5_out, and_6_out, and_7_out, and_8_out, and_9_out,
       and_10_out, and_11_out, and_12_out, and_13_out, and_14_out, and_15_out, and_16_out, and_17_out,
       and_18_out, and_19_out, and_20_out, and_21_out, and_22_out, and_23_out, and_24_out, and_25_out,
       and_26_out, and_27_out, and_28_out, and_29_out, and_30_out, and_31_out, and_32_out, and_33_out,
       and_34_out, and_35_out, and_36_out, and_37_out, and_38_out, and_39_out, and_40_out, and_41_out,
       and_42_out, and_43_out, and_44_out, and_45_out, and_46_out, and_47_out, and_48_out, and_49_out,
       and_50_out, and_51_out, and_52_out, and_53_out, and_54_out, and_55_out, and_56_out, and_57_out,
       and_58_out, and_59_out, and_60_out, and_61_out, and_62_out, and_63_out, and_64_out, and_65_out,
       and_66_out, and_67_out, and_68_out, and_69_out, or_1_out, or_2_out, or_3_out, or_4_out, or_5_out,
       or_6_out, or_7_out, or_8_out, or_9_out, or_10_out, or_11_out, or_12_out, or_13_out, or_14_out,
       or_15_out, or_16_out, or_17_out, or_18_out, or_19_out, or_20_out, or_21_out, xnor_1_out, xnor_2_out,
       xnor_3_out, xnor_4_out, xnor_5_out, xnor_6_out, xnor_7_out, xnor_8_out, xnor_9_out, xnor_10_out,
       xnor_11_out, xnor_12_out, xnor_13_out, xnor_14_out, xnor_15_out, xnor_16_out, xnor_17_out,
       xnor_18_out, xor_1_out, xor_2_out, xor_3_out, xor_4_out, xor_5_out, xor_6_out, xor_7_out, xor_8_out,
       xor_9_out, xor_10_out, xor_11_out, xor_12_out, xor_13_out, xor_14_out, xor_15_out, xor_16_out,
       xor_17_out, xor_18_out, xor_19_out, xor_20_out, xor_21_out, xor_22_out, xor_23_out, xor_24_out,
       xor_25_out, xor_26_out, xor_27_out, xor_28_out, xor_29_out, xor_30_out, xor_31_out, xor_32_out,
       xor_33_out, xor_34_out, xor_35_out, xor_36_out, xor_37_out, xor_38_out, xor_39_out, xor_40_out,
       xor_41_out, xor_42_out, xor_43_out, xor_44_out, xor_45_out, xor_46_out, xor_47_out, xor_48_out,
       xor_49_out, xor_50_out, xor_51_out, xor_52_out, xor_53_out, xor_54_out;

  LED led_1 (.in(or_1_out));
  LED led_2 (.in(or_2_out));
  LED led_3 (.in(or_3_out));
  or or_1 (or_1_out, and_1_out, and_2_out);
  or or_2 (or_2_out, and_3_out, and_4_out);
  or or_3 (or_3_out, and_5_out, and_6_out);
  and and_1 (and_1_out, xor_1_out, or_4_out);
  and and_2 (and_2_out, in_1, xor_2_out);
  and and_3 (and_3_out, xor_3_out, or_5_out);
  and and_4 (and_4_out, in_1, xor_4_out);
  and and_5 (and_5_out, xor_5_out, or_6_out);
  and and_6 (and_6_out, in_1, xor_6_out);
  xor xor_1 (xor_1_out, and_7_out, or_4_out);
  xor xor_2 (xor_2_out, in_1, in_7);
  xor xor_3 (xor_3_out, and_8_out, or_5_out);
  xor xor_4 (xor_4_out, in_1, in_7);
  xor xor_5 (xor_5_out, and_9_out, or_6_out);
  xor xor_6 (xor_6_out, in_1, in_7);
  and and_7 (and_7_out, xor_7_out, in_7);
  and and_8 (and_8_out, xor_8_out, in_7);
  and and_9 (and_9_out, xor_9_out, in_7);
  xor xor_7 (xor_7_out, in_1, in_7);
  xor xor_8 (xor_8_out, in_1, in_7);
  xor xor_9 (xor_9_out, in_1, in_7);
  LED led_4 (.in(or_1_out));
  LED led_5 (.in(or_2_out));
  LED led_6 (.in(or_3_out));
  LED led_7 (.in(or_4_out));
  LED led_8 (.in(or_5_out));
  LED led_9 (.in(or_6_out));
  or or_4 (or_4_out, and_10_out, and_11_out);
  or or_5 (or_5_out, and_12_out, and_13_out);
  or or_6 (or_6_out, and_14_out, and_15_out);
  LED led_10 (.in(or_7_out));
  and and_10 (and_10_out, xor_10_out, or_10_out);
  and and_11 (and_11_out, in_2, xor_11_out);
  LED led_11 (.in(or_8_out));
  and and_12 (and_12_out, xor_12_out, or_11_out);
  and and_13 (and_13_out, in_2, xor_13_out);
  LED led_12 (.in(or_9_out));
  and and_14 (and_14_out, xor_14_out, or_12_out);
  and and_15 (and_15_out, in_2, xor_15_out);
  xor xor_10 (xor_10_out, and_16_out, or_10_out);
  xor xor_11 (xor_11_out, in_2, 1'b0);
  xor xor_12 (xor_12_out, and_17_out, or_11_out);
  xor xor_13 (xor_13_out, in_2, in_8);
  xor xor_14 (xor_14_out, and_18_out, or_12_out);
  xor xor_15 (xor_15_out, in_2, in_8);
  and and_16 (and_16_out, xor_16_out, 1'b0);
  and and_17 (and_17_out, xor_17_out, in_8);
  and and_18 (and_18_out, xor_18_out, in_8);
  or or_7 (or_7_out, or_1_out, and_40_out);
  or or_8 (or_8_out, or_2_out, and_41_out);
  or or_9 (or_9_out, or_3_out, and_42_out);
  xor xor_16 (xor_16_out, in_2, 1'b0);
  xor xor_17 (xor_17_out, in_2, in_8);
  xor xor_18 (xor_18_out, in_2, in_8);
  LED led_13 (.in(or_10_out));
  LED led_14 (.in(or_11_out));
  LED led_15 (.in(or_12_out));
  or or_10 (or_10_out, and_19_out, and_20_out);
  or or_11 (or_11_out, and_21_out, and_22_out);
  or or_12 (or_12_out, and_23_out, and_24_out);
  xnor xnor_1 (xnor_1_out, in_6, 1'b0);
  xnor xnor_2 (xnor_2_out, in_5, 1'b0);
  xnor xnor_3 (xnor_3_out, in_4, 1'b0);
  xnor xnor_4 (xnor_4_out, in_3, 1'b0);
  xnor xnor_5 (xnor_5_out, in_2, 1'b0);
  xnor xnor_6 (xnor_6_out, in_1, in_7);
  and and_19 (and_19_out, xor_19_out, or_13_out);
  and and_20 (and_20_out, in_3, xor_20_out);
  xnor xnor_7 (xnor_7_out, in_6, 1'b0);
  xnor xnor_8 (xnor_8_out, in_5, 1'b0);
  xnor xnor_9 (xnor_9_out, in_4, 1'b0);
  xnor xnor_10 (xnor_10_out, in_3, 1'b0);
  xnor xnor_11 (xnor_11_out, in_2, in_8);
  xnor xnor_12 (xnor_12_out, in_1, in_7);
  and and_21 (and_21_out, xor_21_out, or_14_out);
  and and_22 (and_22_out, in_3, xor_22_out);
  xnor xnor_13 (xnor_13_out, in_6, 1'b0);
  xnor xnor_14 (xnor_14_out, in_5, 1'b0);
  xnor xnor_15 (xnor_15_out, in_4, 1'b0);
  xnor xnor_16 (xnor_16_out, in_3, in_9);
  xnor xnor_17 (xnor_17_out, in_2, in_8);
  xnor xnor_18 (xnor_18_out, in_1, in_7);
  and and_23 (and_23_out, xor_23_out, or_15_out);
  and and_24 (and_24_out, in_3, xor_24_out);
  xor xor_19 (xor_19_out, and_29_out, or_13_out);
  xor xor_20 (xor_20_out, in_3, 1'b0);
  xor xor_21 (xor_21_out, and_31_out, or_14_out);
  xor xor_22 (xor_22_out, in_3, 1'b0);
  xor xor_23 (xor_23_out, and_33_out, or_15_out);
  xor xor_24 (xor_24_out, in_3, in_9);
  and and_25 (and_25_out, xnor_1_out, xnor_2_out);
  and and_26 (and_26_out, xnor_7_out, xnor_8_out);
  and and_27 (and_27_out, xnor_13_out, xnor_14_out);
  and and_28 (and_28_out, and_25_out, xnor_3_out);
  and and_29 (and_29_out, xor_25_out, 1'b0);
  and and_30 (and_30_out, and_26_out, xnor_9_out);
  and and_31 (and_31_out, xor_26_out, 1'b0);
  and and_32 (and_32_out, and_27_out, xnor_15_out);
  and and_33 (and_33_out, xor_27_out, in_9);
  and and_34 (and_34_out, and_28_out, xnor_4_out);
  xor xor_25 (xor_25_out, in_3, 1'b0);
  and and_35 (and_35_out, and_30_out, xnor_10_out);
  xor xor_26 (xor_26_out, in_3, 1'b0);
  and and_36 (and_36_out, and_32_out, xnor_16_out);
  xor xor_27 (xor_27_out, in_3, in_9);
  and and_37 (and_37_out, and_34_out, xnor_5_out);
  and and_38 (and_38_out, and_35_out, xnor_11_out);
  and and_39 (and_39_out, and_36_out, xnor_17_out);
  and and_40 (and_40_out, and_37_out, xnor_6_out);
  LED led_16 (.in(or_13_out));
  and and_41 (and_41_out, and_38_out, xnor_12_out);
  LED led_17 (.in(or_14_out));
  and and_42 (and_42_out, and_39_out, xnor_18_out);
  LED led_18 (.in(or_15_out));
  or or_13 (or_13_out, and_43_out, and_44_out);
  or or_14 (or_14_out, and_45_out, and_46_out);
  or or_15 (or_15_out, and_47_out, and_48_out);
  and and_43 (and_43_out, xor_28_out, or_16_out);
  and and_44 (and_44_out, in_4, xor_29_out);
  and and_45 (and_45_out, xor_30_out, or_17_out);
  and and_46 (and_46_out, in_4, xor_31_out);
  and and_47 (and_47_out, xor_32_out, or_18_out);
  and and_48 (and_48_out, in_4, xor_33_out);
  xor xor_28 (xor_28_out, and_49_out, or_16_out);
  xor xor_29 (xor_29_out, in_4, 1'b0);
  xor xor_30 (xor_30_out, and_50_out, or_17_out);
  xor xor_31 (xor_31_out, in_4, 1'b0);
  xor xor_32 (xor_32_out, and_51_out, or_18_out);
  xor xor_33 (xor_33_out, in_4, 1'b0);
  and and_49 (and_49_out, xor_34_out, 1'b0);
  and and_50 (and_50_out, xor_35_out, 1'b0);
  and and_51 (and_51_out, xor_36_out, 1'b0);
  xor xor_34 (xor_34_out, in_4, 1'b0);
  xor xor_35 (xor_35_out, in_4, 1'b0);
  xor xor_36 (xor_36_out, in_4, 1'b0);
  LED led_19 (.in(or_16_out));
  LED led_20 (.in(or_17_out));
  LED led_21 (.in(or_18_out));
  or or_16 (or_16_out, and_52_out, and_53_out);
  or or_17 (or_17_out, and_54_out, and_55_out);
  or or_18 (or_18_out, and_56_out, and_57_out);
  and and_52 (and_52_out, xor_37_out, or_19_out);
  and and_53 (and_53_out, in_5, xor_38_out);
  and and_54 (and_54_out, xor_39_out, or_20_out);
  and and_55 (and_55_out, in_5, xor_40_out);
  and and_56 (and_56_out, xor_41_out, or_21_out);
  and and_57 (and_57_out, in_5, xor_42_out);
  xor xor_37 (xor_37_out, and_58_out, or_19_out);
  xor xor_38 (xor_38_out, in_5, 1'b0);
  xor xor_39 (xor_39_out, and_59_out, or_20_out);
  xor xor_40 (xor_40_out, in_5, 1'b0);
  xor xor_41 (xor_41_out, and_60_out, or_21_out);
  xor xor_42 (xor_42_out, in_5, 1'b0);
  and and_58 (and_58_out, xor_43_out, 1'b0);
  and and_59 (and_59_out, xor_44_out, 1'b0);
  and and_60 (and_60_out, xor_45_out, 1'b0);
  xor xor_43 (xor_43_out, in_5, 1'b0);
  xor xor_44 (xor_44_out, in_5, 1'b0);
  xor xor_45 (xor_45_out, in_5, 1'b0);
  LED led_22 (.in(or_19_out));
  LED led_23 (.in(or_20_out));
  LED led_24 (.in(or_21_out));
  or or_19 (or_19_out, and_61_out, and_62_out);
  or or_20 (or_20_out, and_63_out, and_64_out);
  or or_21 (or_21_out, and_65_out, and_66_out);
  and and_61 (and_61_out, xor_46_out, in_13);
  and and_62 (and_62_out, in_6, xor_47_out);
  and and_63 (and_63_out, xor_48_out, in_14);
  and and_64 (and_64_out, in_6, xor_49_out);
  and and_65 (and_65_out, xor_50_out, in_15);
  and and_66 (and_66_out, in_6, xor_51_out);
  xor xor_46 (xor_46_out, and_67_out, in_13);
  xor xor_47 (xor_47_out, in_6, 1'b0);
  xor xor_48 (xor_48_out, and_68_out, in_14);
  xor xor_49 (xor_49_out, in_6, 1'b0);
  xor xor_50 (xor_50_out, and_69_out, in_15);
  xor xor_51 (xor_51_out, in_6, 1'b0);
  and and_67 (and_67_out, xor_52_out, 1'b0);
  and and_68 (and_68_out, xor_53_out, 1'b0);
  and and_69 (and_69_out, xor_54_out, 1'b0);
  xor xor_52 (xor_52_out, in_6, 1'b0);
  xor xor_53 (xor_53_out, in_6, 1'b0);
  xor xor_54 (xor_54_out, in_6, 1'b0);
endmodule
