// Logisim project instructor.circ as structural Verilog: 1 circuit, main circuit main
module main (
  input  in_1,
  input  in_2,
  input  in_3,
  input  in_4,
  output ADD,
  output INVERT,
  output A_B,
  output A_B_2,
  output A_B_3,
  output STEP,
  output INSERT,
  output OUT,
  output HALT,
  output out_14,
  output out_15,
  output out_16
);

  wire and_1_out, and_2_out, and_3_out, and_4_out, and_5_out, and_6_out, and_7_out, and_8_out, and_9_out,
       and_10_out, and_11_out, and_12_out, and_13_out, and_14_out, and_15_out, and_16_out, and_17_out,
       and_18_out, and_19_out, and_20_out, and_21_out, and_22_out, and_23_out, and_24_out, xnor_1_out,
       xnor_2_out, xnor_3_out, xnor_4_out, xnor_5_out, xnor_6_out, xnor_7_out, xnor_8_out, xnor_9_out,
       xnor_10_out, xnor_11_out, xnor_12_out, xnor_13_out, xnor_14_out, xnor_15_out, xnor_16_out,
       xnor_17_out, xnor_18_out, xnor_19_out, xnor_20_out, xnor_21_out, xnor_22_out, xnor_23_out,
       xnor_24_out, xnor_25_out, xnor_26_out, xnor_27_out, xnor_28_out, xnor_29_out, xnor_30_out,
       xnor_31_out, xnor_32_out, xnor_33_out, xnor_34_out, xnor_35_out, xnor_36_out, xnor_37_out,
       xnor_38_out, xnor_39_out, xnor_40_out, xnor_41_out, xnor_42_out, xnor_43_out, xnor_44_out,
       xnor_45_out, xnor_46_out, xnor_47_out, xnor_48_out;

  xnor xnor_1 (xnor_1_out, 1'b1, in_4);
  xnor xnor_2 (xnor_2_out, 1'b0, in_3);
  xnor xnor_3 (xnor_3_out, 1'b0, in_2);
  xnor xnor_4 (xnor_4_out, 1'b0, in_1);
  xnor xnor_5 (xnor_5_out, 1'b0, in_4);
  xnor xnor_6 (xnor_6_out, 1'b1, in_3);
  xnor xnor_7 (xnor_7_out, 1'b0, in_2);
  xnor xnor_8 (xnor_8_out, 1'b0, in_1);
  xnor xnor_9 (xnor_9_out, 1'b1, in_4);
  xnor xnor_10 (xnor_10_out, 1'b1, in_3);
  xnor xnor_11 (xnor_11_out, 1'b0, in_2);
  xnor xnor_12 (xnor_12_out, 1'b0, in_1);
  xnor xnor_13 (xnor_13_out, 1'b0, in_4);
  xnor xnor_14 (xnor_14_out, 1'b0, in_3);
  xnor xnor_15 (xnor_15_out, 1'b1, in_2);
  xnor xnor_16 (xnor_16_out, 1'b0, in_1);
  xnor xnor_17 (xnor_17_out, 1'b1, in_4);
  xnor xnor_18 (xnor_18_out, 1'b0, in_3);
  xnor xnor_19 (xnor_19_out, 1'b1, in_2);
  xnor xnor_20 (xnor_20_out, 1'b0, in_1);
  xnor xnor_21 (xnor_21_out, 1'b0, in_4);
  xnor xnor_22 (xnor_22_out, 1'b1, in_3);
  xnor xnor_23 (xnor_23_out, 1'b1, in_2);
  xnor xnor_24 (xnor_24_out, 1'b0, in_1);
  xnor xnor_25 (xnor_25_out, 1'b1, in_4);
  xnor xnor_26 (xnor_26_out, 1'b1, in_3);
  xnor xnor_27 (xnor_27_out, 1'b1, in_2);
  xnor xnor_28 (xnor_28_out, 1'b0, in_1);
  xnor xnor_29 (xnor_29_out, 1'b0, in_4);
  xnor xnor_30 (xnor_30_out, 1'b0, in_3);
  xnor xnor_31 (xnor_31_out, 1'b0, in_2);
  xnor xnor_32 (xnor_32_out, 1'b1, in_1);
  xnor xnor_33 (xnor_33_out, 1'b1, in_4);
  xnor xnor_34 (xnor_34_out, 1'b0, in_3);
  xnor xnor_35 (xnor_35_out, 1'b0, in_2);
  xnor xnor_36 (xnor_36_out, 1'b1, in_1);
  xnor xnor_37 (xnor_37_out, 1'b0, in_4);
  xnor xnor_38 (xnor_38_out, 1'b1, in_3);
  xnor xnor_39 (xnor_39_out, 1'b0, in_2);
  xnor xnor_40 (xnor_40_out, 1'b1, in_1);
  xnor xnor_41 (xnor_41_out, 1'b1, in_4);
  xnor xnor_42 (xnor_42_out, 1'b1, in_3);
  xnor xnor_43 (xnor_43_out, 1'b0, in_2);
  xnor xnor_44 (xnor_44_out, 1'b1, in_1);
  xnor xnor_45 (xnor_45_out, 1'b0, in_4);
  xnor xnor_46 (xnor_46_out, 1'b0, in_3);
  xnor xnor_47 (xnor_47_out, 1'b1, in_2);
  xnor xnor_48 (xnor_48_out, 1'b1, in_1);
  and and_1 (and_1_out, xnor_1_out, xnor_2_out);
  and and_2 (and_2_out, xnor_5_out, xnor_6_out);
  and and_3 (and_3_out, xnor_9_out, xnor_10_out);
  and and_4 (and_4_out, xnor_13_out, xnor_14_out);
  and and_5 (and_5_out, xnor_17_out, xnor_18_out);
  and and_6 (and_6_out, xnor_21_out, xnor_22_out);
  and and_7 (and_7_out, xnor_25_out, xnor_26_out);
  and and_8 (and_8_out, xnor_29_out, xnor_30_out);
  and and_9 (and_9_out, xnor_33_out, xnor_34_out);
  and and_10 (and_10_out, xnor_37_out, xnor_38_out);
  and and_11 (and_11_out, xnor_41_out, xnor_42_out);
  and and_12 (and_12_out, xnor_45_out, xnor_46_out);
  and and_13 (and_13_out, and_1_out, xnor_3_out);
  and and_14 (and_14_out, and_2_out, xnor_7_out);
  and and_15 (and_15_out, and_3_out, xnor_11_out);
  and and_16 (and_16_out, and_4_out, xnor_15_out);
  and and_17 (and_17_out, and_5_out, xnor_19_out);
  and and_18 (and_18_out, and_6_out, xnor_23_out);
  and and_19 (and_19_out, and_7_out, xnor_27_out);
  and and_20 (and_20_out, and_8_out, xnor_31_out);
  and and_21 (and_21_out, and_9_out, xnor_35_out);
  and and_22 (and_22_out, and_10_out, xnor_39_out);
  and and_23 (and_23_out, and_11_out, xnor_43_out);
  and and_24 (and_24_out, and_12_out, xnor_47_out);
  and and_25 (ADD, and_13_out, xnor_4_out);
  and and_26 (INVERT, and_14_out, xnor_8_out);
  and and_27 (A_B, and_15_out, xnor_12_out);
  and and_28 (A_B_2, and_16_out, xnor_16_out);
  and and_29 (A_B_3, and_17_out, xnor_20_out);
  and and_30 (STEP, and_18_out, xnor_24_out);
  and and_31 (INSERT, and_19_out, xnor_28_out);
  and and_32 (OUT, and_20_out, xnor_32_out);
  and and_33 (HALT, and_21_out, xnor_36_out);
  and and_34 (out_14, and_22_out, xnor_40_out);
  and and_35 (out_15, and_23_out, xnor_44_out);
  and and_36 (out_16, and_24_out, xnor_48_out);

  // Notes on the sheet:
  //   Input
endmodule
