// Logisim project memory.circ as structural Verilog: 1 circuit, main circuit main
module main (
  input  in_1,
  input  in_2,
  input  in_3,
  input  in_4,
  input  in_5,
  input  in_6
);

  wire and_1_out, and_2_out, and_3_out, and_4_out, and_10_out, and_11_out, and_17_out, and_18_out,
       and_24_out, and_25_out, and_31_out, and_37_out, button_1_out, button_2_out, nand_1_out, nand_2_out,
       nand_3_out, nand_4_out, nand_5_out, nand_6_out, nand_7_out, nand_8_out, nand_9_out, nand_10_out,
       nand_11_out, nand_12_out, nand_13_out, nand_14_out, nand_15_out, nand_16_out, nand_17_out,
       nand_18_out, nand_19_out, nand_20_out, nand_21_out, nand_22_out, nand_23_out, nand_24_out,
       nand_25_out, nand_26_out, nand_27_out, nand_28_out, nand_29_out, nand_30_out, nand_31_out,
       nand_32_out, nand_33_out, nand_34_out, nand_35_out, nand_36_out, nand_37_out, nand_38_out,
       nand_39_out, nand_40_out, nand_41_out, nand_42_out, nand_43_out, nand_44_out, nand_45_out,
       nand_46_out, nand_47_out, nand_48_out, nand_49_out, nand_50_out, nand_51_out, nand_52_out,
       nand_53_out, nand_54_out, nand_55_out, nand_56_out, nand_57_out, nand_58_out, nand_59_out,
       nand_60_out, nand_61_out, nand_62_out, nand_63_out, nand_64_out, nand_65_out, nand_66_out,
       nand_67_out, nand_68_out, nand_69_out, nand_70_out, nand_71_out, nand_72_out, nand_73_out,
       nand_74_out, nand_75_out, nand_76_out, nand_77_out, nand_78_out, nand_79_out, nand_80_out,
       nand_81_out, nand_82_out, nand_83_out, nand_84_out, nand_85_out, nand_86_out, nand_87_out,
       nand_88_out, nand_89_out, nand_90_out, nand_91_out, nand_92_out, nand_93_out, nand_94_out,
       nand_95_out, nand_96_out, nand_97_out, nand_98_out, nand_99_out, nand_100_out, nand_101_out,
       nand_102_out, nand_103_out, nand_104_out, nand_105_out, nand_106_out, nand_107_out, nand_108_out,
       nand_109_out, nand_110_out, nand_111_out, nand_112_out, nand_113_out, nand_114_out, nand_115_out,
       nand_116_out, nand_117_out, nand_118_out, nand_119_out, nand_120_out, nand_121_out, nand_122_out,
       nand_123_out, nand_124_out, nand_125_out, nand_126_out, nand_127_out, nand_128_out, nand_129_out,
       nand_130_out, nand_131_out, nand_132_out, nand_133_out, nand_134_out, nand_135_out, nand_136_out,
       nand_137_out, nand_138_out, nand_139_out, nand_140_out, nand_141_out, nand_142_out, nand_143_out,
       nand_144_out, nand_145_out, nand_146_out, nand_147_out, nand_148_out, nand_149_out, nand_150_out,
       nand_151_out, nand_152_out, nand_153_out, nand_154_out, nand_155_out, nand_156_out, nand_157_out,
       nand_158_out, nand_159_out, nand_160_out, nand_161_out, nand_162_out, nand_163_out, nand_164_out,
       nand_165_out, nand_166_out, nand_167_out, nand_168_out, not_1_out, not_2_out, not_3_out, not_4_out,
       not_5_out, not_6_out, not_7_out, not_8_out, not_9_out, not_10_out, not_11_out, not_12_out, not_13_out,
       not_14_out, not_15_out, not_16_out, not_17_out, not_18_out, not_19_out, not_20_out, not_21_out,
       not_22_out, not_23_out, not_24_out, not_25_out, not_26_out, not_27_out, not_28_out, not_29_out,
       not_30_out, not_31_out, not_32_out, not_33_out, not_34_out, not_35_out, not_36_out, not_37_out,
       not_38_out, not_39_out, not_40_out, not_41_out, not_42_out, undriven, undriven_2, undriven_3,
       undriven_4, undriven_5, undriven_6, undriven_7, undriven_8, undriven_9, undriven_10, undriven_11,
       undriven_12, undriven_13, undriven_14, undriven_15, undriven_16, undriven_17, undriven_18;

  Button button_1 (.out(button_1_out));
  LED led_1 (.in(and_24_out));
  LED led_2 (.in(and_17_out));
  LED led_3 (.in(and_10_out));
  LED led_4 (.in(and_3_out));
  LED led_5 (.in(and_2_out));
  LED led_6 (.in(and_1_out));
  Button button_2 (.out(button_2_out));
  not not_1 (not_1_out, in_6);
  nand nand_1 (nand_1_out, not_1_out, button_2_out);
  nand nand_2 (nand_2_out, button_2_out, in_6);
  nand nand_3 (nand_3_out, nand_1_out, nand_4_out);
  nand nand_4 (nand_4_out, nand_3_out, nand_2_out);
  and and_1 (and_1_out, button_1_out, nand_4_out);
  not not_2 (not_2_out, in_5);
  nand nand_5 (nand_5_out, not_2_out, button_2_out);
  nand nand_6 (nand_6_out, button_2_out, in_5);
  nand nand_7 (nand_7_out, nand_5_out, nand_8_out);
  nand nand_8 (nand_8_out, nand_7_out, nand_6_out);
  and and_2 (and_2_out, button_1_out, nand_8_out);
  not not_3 (not_3_out, in_4);
  nand nand_9 (nand_9_out, not_3_out, button_2_out);
  nand nand_10 (nand_10_out, button_2_out, in_4);
  not not_4 (not_4_out, undriven_7);
  not not_5 (not_5_out, undriven_7);
  not not_6 (not_6_out, undriven_7);
  not not_7 (not_7_out, undriven_7);
  not not_8 (not_8_out, undriven_7);
  not not_9 (not_9_out, undriven_7);
  nand nand_11 (nand_11_out, not_4_out, undriven);
  nand nand_12 (nand_12_out, undriven, undriven_7);
  nand nand_13 (nand_13_out, not_5_out, undriven_2);
  nand nand_14 (nand_14_out, undriven_2, undriven_7);
  nand nand_15 (nand_15_out, not_6_out, undriven_3);
  nand nand_16 (nand_16_out, undriven_3, undriven_7);
  nand nand_17 (nand_17_out, not_7_out, undriven_4);
  nand nand_18 (nand_18_out, undriven_4, undriven_7);
  nand nand_19 (nand_19_out, not_8_out, undriven_5);
  nand nand_20 (nand_20_out, undriven_5, undriven_7);
  nand nand_21 (nand_21_out, not_9_out, undriven_6);
  nand nand_22 (nand_22_out, undriven_6, undriven_7);
  nand nand_23 (nand_23_out, nand_9_out, nand_24_out);
  nand nand_24 (nand_24_out, nand_23_out, nand_10_out);
  nand nand_25 (nand_25_out, nand_11_out, nand_26_out);
  nand nand_26 (nand_26_out, nand_25_out, nand_12_out);
  nand nand_27 (nand_27_out, nand_13_out, nand_28_out);
  nand nand_28 (nand_28_out, nand_27_out, nand_14_out);
  nand nand_29 (nand_29_out, nand_15_out, nand_30_out);
  nand nand_30 (nand_30_out, nand_29_out, nand_16_out);
  nand nand_31 (nand_31_out, nand_17_out, nand_32_out);
  nand nand_32 (nand_32_out, nand_31_out, nand_18_out);
  nand nand_33 (nand_33_out, nand_19_out, nand_34_out);
  nand nand_34 (nand_34_out, nand_33_out, nand_20_out);
  nand nand_35 (nand_35_out, nand_21_out, nand_36_out);
  nand nand_36 (nand_36_out, nand_35_out, nand_22_out);
  and and_3 (and_3_out, button_1_out, nand_24_out);
  and and_4 (and_4_out, undriven_13, nand_26_out);
  and and_5 (and_4_out, undriven_14, nand_28_out);
  and and_6 (and_4_out, undriven_15, nand_30_out);
  and and_7 (and_4_out, undriven_16, nand_32_out);
  and and_8 (and_4_out, undriven_17, nand_34_out);
  and and_9 (and_4_out, undriven_18, nand_36_out);
  not not_10 (not_10_out, in_3);
  nand nand_37 (nand_37_out, not_10_out, button_2_out);
  nand nand_38 (nand_38_out, button_2_out, in_3);
  not not_11 (not_11_out, undriven_8);
  not not_12 (not_12_out, undriven_8);
  not not_13 (not_13_out, undriven_8);
  not not_14 (not_14_out, undriven_8);
  not not_15 (not_15_out, undriven_8);
  not not_16 (not_16_out, undriven_8);
  nand nand_39 (nand_39_out, not_11_out, undriven);
  nand nand_40 (nand_40_out, undriven, undriven_8);
  nand nand_41 (nand_41_out, not_12_out, undriven_2);
  nand nand_42 (nand_42_out, undriven_2, undriven_8);
  nand nand_43 (nand_43_out, not_13_out, undriven_3);
  nand nand_44 (nand_44_out, undriven_3, undriven_8);
  nand nand_45 (nand_45_out, not_14_out, undriven_4);
  nand nand_46 (nand_46_out, undriven_4, undriven_8);
  nand nand_47 (nand_47_out, not_15_out, undriven_5);
  nand nand_48 (nand_48_out, undriven_5, undriven_8);
  nand nand_49 (nand_49_out, not_16_out, undriven_6);
  nand nand_50 (nand_50_out, undriven_6, undriven_8);
  nand nand_51 (nand_51_out, nand_37_out, nand_52_out);
  nand nand_52 (nand_52_out, nand_51_out, nand_38_out);
  nand nand_53 (nand_53_out, nand_39_out, nand_54_out);
  nand nand_54 (nand_54_out, nand_53_out, nand_40_out);
  nand nand_55 (nand_55_out, nand_41_out, nand_56_out);
  nand nand_56 (nand_56_out, nand_55_out, nand_42_out);
  nand nand_57 (nand_57_out, nand_43_out, nand_58_out);
  nand nand_58 (nand_58_out, nand_57_out, nand_44_out);
  nand nand_59 (nand_59_out, nand_45_out, nand_60_out);
  nand nand_60 (nand_60_out, nand_59_out, nand_46_out);
  nand nand_61 (nand_61_out, nand_47_out, nand_62_out);
  nand nand_62 (nand_62_out, nand_61_out, nand_48_out);
  nand nand_63 (nand_63_out, nand_49_out, nand_64_out);
  nand nand_64 (nand_64_out, nand_63_out, nand_50_out);
  and and_10 (and_10_out, button_1_out, nand_52_out);
  and and_11 (and_11_out, undriven_13, nand_54_out);
  and and_12 (and_11_out, undriven_14, nand_56_out);
  and and_13 (and_11_out, undriven_15, nand_58_out);
  and and_14 (and_11_out, undriven_16, nand_60_out);
  and and_15 (and_11_out, undriven_17, nand_62_out);
  and and_16 (and_11_out, undriven_18, nand_64_out);
  not not_17 (not_17_out, in_2);
  not not_18 (not_18_out, undriven_9);
  not not_19 (not_19_out, undriven_9);
  not not_20 (not_20_out, undriven_9);
  not not_21 (not_21_out, undriven_9);
  not not_22 (not_22_out, undriven_9);
  not not_23 (not_23_out, undriven_9);
  nand nand_65 (nand_65_out, not_17_out, button_2_out);
  nand nand_66 (nand_66_out, button_2_out, in_2);
  nand nand_67 (nand_67_out, not_18_out, undriven);
  nand nand_68 (nand_68_out, undriven, undriven_9);
  nand nand_69 (nand_69_out, not_19_out, undriven_2);
  nand nand_70 (nand_70_out, undriven_2, undriven_9);
  nand nand_71 (nand_71_out, not_20_out, undriven_3);
  nand nand_72 (nand_72_out, undriven_3, undriven_9);
  nand nand_73 (nand_73_out, not_21_out, undriven_4);
  nand nand_74 (nand_74_out, undriven_4, undriven_9);
  nand nand_75 (nand_75_out, not_22_out, undriven_5);
  nand nand_76 (nand_76_out, undriven_5, undriven_9);
  nand nand_77 (nand_77_out, not_23_out, undriven_6);
  nand nand_78 (nand_78_out, undriven_6, undriven_9);
  nand nand_79 (nand_79_out, nand_65_out, nand_80_out);
  nand nand_80 (nand_80_out, nand_79_out, nand_66_out);
  nand nand_81 (nand_81_out, nand_67_out, nand_82_out);
  nand nand_82 (nand_82_out, nand_81_out, nand_68_out);
  nand nand_83 (nand_83_out, nand_69_out, nand_84_out);
  nand nand_84 (nand_84_out, nand_83_out, nand_70_out);
  nand nand_85 (nand_85_out, nand_71_out, nand_86_out);
  nand nand_86 (nand_86_out, nand_85_out, nand_72_out);
  nand nand_87 (nand_87_out, nand_73_out, nand_88_out);
  nand nand_88 (nand_88_out, nand_87_out, nand_74_out);
  nand nand_89 (nand_89_out, nand_75_out, nand_90_out);
  nand nand_90 (nand_90_out, nand_89_out, nand_76_out);
  nand nand_91 (nand_91_out, nand_77_out, nand_92_out);
  nand nand_92 (nand_92_out, nand_91_out, nand_78_out);
  and and_17 (and_17_out, button_1_out, nand_80_out);
  and and_18 (and_18_out, undriven_13, nand_82_out);
  and and_19 (and_18_out, undriven_14, nand_84_out);
  and and_20 (and_18_out, undriven_15, nand_86_out);
  and and_21 (and_18_out, undriven_16, nand_88_out);
  and and_22 (and_18_out, undriven_17, nand_90_out);
  and and_23 (and_18_out, undriven_18, nand_92_out);
  not not_24 (not_24_out, in_1);
  nand nand_93 (nand_93_out, not_24_out, button_2_out);
  nand nand_94 (nand_94_out, button_2_out, in_1);
  not not_25 (not_25_out, undriven_10);
  nand nand_95 (nand_95_out, not_25_out, undriven);
  nand nand_96 (nand_96_out, undriven, undriven_10);
  not not_26 (not_26_out, undriven_10);
  nand nand_97 (nand_97_out, not_26_out, undriven_2);
  nand nand_98 (nand_98_out, undriven_2, undriven_10);
  not not_27 (not_27_out, undriven_10);
  nand nand_99 (nand_99_out, not_27_out, undriven_3);
  nand nand_100 (nand_100_out, undriven_3, undriven_10);
  not not_28 (not_28_out, undriven_10);
  nand nand_101 (nand_101_out, not_28_out, undriven_4);
  nand nand_102 (nand_102_out, undriven_4, undriven_10);
  not not_29 (not_29_out, undriven_10);
  nand nand_103 (nand_103_out, not_29_out, undriven_5);
  nand nand_104 (nand_104_out, undriven_5, undriven_10);
  not not_30 (not_30_out, undriven_10);
  nand nand_105 (nand_105_out, not_30_out, undriven_6);
  nand nand_106 (nand_106_out, undriven_6, undriven_10);
  nand nand_107 (nand_107_out, nand_93_out, nand_108_out);
  nand nand_108 (nand_108_out, nand_107_out, nand_94_out);
  nand nand_109 (nand_109_out, nand_95_out, nand_110_out);
  nand nand_110 (nand_110_out, nand_109_out, nand_96_out);
  nand nand_111 (nand_111_out, nand_97_out, nand_112_out);
  nand nand_112 (nand_112_out, nand_111_out, nand_98_out);
  nand nand_113 (nand_113_out, nand_99_out, nand_114_out);
  nand nand_114 (nand_114_out, nand_113_out, nand_100_out);
  nand nand_115 (nand_115_out, nand_101_out, nand_116_out);
  nand nand_116 (nand_116_out, nand_115_out, nand_102_out);
  nand nand_117 (nand_117_out, nand_103_out, nand_118_out);
  nand nand_118 (nand_118_out, nand_117_out, nand_104_out);
  nand nand_119 (nand_119_out, nand_105_out, nand_120_out);
  nand nand_120 (nand_120_out, nand_119_out, nand_106_out);
  and and_24 (and_24_out, button_1_out, nand_108_out);
  and and_25 (and_25_out, undriven_13, nand_110_out);
  and and_26 (and_25_out, undriven_14, nand_112_out);
  and and_27 (and_25_out, undriven_15, nand_114_out);
  and and_28 (and_25_out, undriven_16, nand_116_out);
  and and_29 (and_25_out, undriven_17, nand_118_out);
  and and_30 (and_25_out, undriven_18, nand_120_out);
  not not_31 (not_31_out, undriven_11);
  not not_32 (not_32_out, undriven_11);
  not not_33 (not_33_out, undriven_11);
  not not_34 (not_34_out, undriven_11);
  not not_35 (not_35_out, undriven_11);
  not not_36 (not_36_out, undriven_11);
  nand nand_121 (nand_121_out, not_31_out, undriven);
  nand nand_122 (nand_122_out, undriven, undriven_11);
  nand nand_123 (nand_123_out, not_32_out, undriven_2);
  nand nand_124 (nand_124_out, undriven_2, undriven_11);
  nand nand_125 (nand_125_out, not_33_out, undriven_3);
  nand nand_126 (nand_126_out, undriven_3, undriven_11);
  nand nand_127 (nand_127_out, not_34_out, undriven_4);
  nand nand_128 (nand_128_out, undriven_4, undriven_11);
  nand nand_129 (nand_129_out, not_35_out, undriven_5);
  nand nand_130 (nand_130_out, undriven_5, undriven_11);
  nand nand_131 (nand_131_out, not_36_out, undriven_6);
  nand nand_132 (nand_132_out, undriven_6, undriven_11);
  nand nand_133 (nand_133_out, nand_121_out, nand_134_out);
  nand nand_134 (nand_134_out, nand_133_out, nand_122_out);
  nand nand_135 (nand_135_out, nand_123_out, nand_136_out);
  nand nand_136 (nand_136_out, nand_135_out, nand_124_out);
  nand nand_137 (nand_137_out, nand_125_out, nand_138_out);
  nand nand_138 (nand_138_out, nand_137_out, nand_126_out);
  nand nand_139 (nand_139_out, nand_127_out, nand_140_out);
  nand nand_140 (nand_140_out, nand_139_out, nand_128_out);
  nand nand_141 (nand_141_out, nand_129_out, nand_142_out);
  nand nand_142 (nand_142_out, nand_141_out, nand_130_out);
  nand nand_143 (nand_143_out, nand_131_out, nand_144_out);
  nand nand_144 (nand_144_out, nand_143_out, nand_132_out);
  and and_31 (and_31_out, undriven_13, nand_134_out);
  and and_32 (and_31_out, undriven_14, nand_136_out);
  and and_33 (and_31_out, undriven_15, nand_138_out);
  and and_34 (and_31_out, undriven_16, nand_140_out);
  and and_35 (and_31_out, undriven_17, nand_142_out);
  and and_36 (and_31_out, undriven_18, nand_144_out);
  not not_37 (not_37_out, undriven_12);
  not not_38 (not_38_out, undriven_12);
  not not_39 (not_39_out, undriven_12);
  not not_40 (not_40_out, undriven_12);
  not not_41 (not_41_out, undriven_12);
  not not_42 (not_42_out, undriven_12);
  nand nand_145 (nand_145_out, not_37_out, undriven);
  nand nand_146 (nand_146_out, undriven, undriven_12);
  nand nand_147 (nand_147_out, not_38_out, undriven_2);
  nand nand_148 (nand_148_out, undriven_2, undriven_12);
  nand nand_149 (nand_149_out, not_39_out, undriven_3);
  nand nand_150 (nand_150_out, undriven_3, undriven_12);
  nand nand_151 (nand_151_out, not_40_out, undriven_4);
  nand nand_152 (nand_152_out, undriven_4, undriven_12);
  nand nand_153 (nand_153_out, not_41_out, undriven_5);
  nand nand_154 (nand_154_out, undriven_5, undriven_12);
  nand nand_155 (nand_155_out, not_42_out, undriven_6);
  nand nand_156 (nand_156_out, undriven_6, undriven_12);
  nand nand_157 (nand_157_out, nand_145_out, nand_158_out);
  nand nand_158 (nand_158_out, nand_157_out, nand_146_out);
  nand nand_159 (nand_159_out, nand_147_out, nand_160_out);
  nand nand_160 (nand_160_out, nand_159_out, nand_148_out);
  nand nand_161 (nand_161_out, nand_149_out, nand_162_out);
  nand nand_162 (nand_162_out, nand_161_out, nand_150_out);
  nand nand_163 (nand_163_out, nand_151_out, nand_164_out);
  nand nand_164 (nand_164_out, nand_163_out, nand_152_out);
  nand nand_165 (nand_165_out, nand_153_out, nand_166_out);
  nand nand_166 (nand_166_out, nand_165_out, nand_154_out);
  nand nand_167 (nand_167_out, nand_155_out, nand_168_out);
  nand nand_168 (nand_168_out, nand_167_out, nand_156_out);
  and and_37 (and_37_out, undriven_13, nand_158_out);
  and and_38 (and_37_out, undriven_14, nand_160_out);
  and and_39 (and_37_out, undriven_15, nand_162_out);
  and and_40 (and_37_out, undriven_16, nand_164_out);
  and and_41 (and_37_out, undriven_17, nand_166_out);
  and and_42 (and_37_out, undriven_18, nand_168_out);
endmodule
