// Logisim project memory_alt.circ as structural Verilog: 1 circuit, main circuit main
module main (
  input  [2:0] in_1,
  input  [2:0] in_2,
  input  [5:0] in_3,
  input  W,
  input  R,
  input  P,
  output [5:0] out_7
);

  wire clock_1_out, not_1_out;
  wire [5:0] and_7_out, and_12_out, controlled_buffer_1_out, ram_1_data;

  Clock clock_1 (.out(clock_1_out));
  and and_1 (and_7_out[5], in_1[2], P);
  RAM #(.addrWidth(3), .dataWidth(6)) ram_1 (
    .addr(in_2), .data(ram_1_data), .sel(1'b1), .clk(clock_1_out), .ld(not_1_out), .clr(1'b0));
  not not_1 (not_1_out, W);
  and and_2 (and_7_out[4], in_1[1], P);
  assign controlled_buffer_1_out = R ? ram_1_data : 6'bz;  // Controlled_Buffer controlled_buffer_1
  assign ram_1_data = W ? in_3 : 6'bz;  // Controlled_Buffer controlled_buffer_2
  or or_1 (out_7[5], and_7_out[5], and_12_out[5]);
  and and_3 (and_7_out[3], in_1[0], P);
  or or_2 (out_7[4], and_7_out[4], and_12_out[4]);
  and and_4 (and_7_out[2], in_2[2], P);
  or or_3 (out_7[3], and_7_out[3], and_12_out[3]);
  and and_5 (and_7_out[1], in_2[1], P);
  and and_6 (and_12_out[5], controlled_buffer_1_out[5], R);
  or or_4 (out_7[2], and_7_out[2], and_12_out[2]);
  and and_7 (and_7_out[0], in_2[0], P);
  and and_8 (and_12_out[4], controlled_buffer_1_out[4], R);
  or or_5 (out_7[1], and_7_out[1], and_12_out[1]);
  and and_9 (and_12_out[3], controlled_buffer_1_out[3], R);
  or or_6 (out_7[0], and_7_out[0], and_12_out[0]);
  and and_10 (and_12_out[2], controlled_buffer_1_out[2], R);
  and and_11 (and_12_out[1], controlled_buffer_1_out[1], R);
  and and_12 (and_12_out[0], controlled_buffer_1_out[0], R);
endmodule
