// Logisim project multiplication.circ as structural Verilog: 1 circuit, main circuit main
module main (
  input  in_1,
  input  in_2,
  input  in_3,
  input  in_4,
  input  in_5,
  input  in_6,
  input  in_7,
  input  in_8,
  input  in_9,
  input  in_10,
  input  in_11,
  input  in_12,
  input  in_13
);

  wire and_1_out, and_2_out, and_3_out, and_4_out, and_5_out, and_6_out, and_7_out, and_8_out, and_9_out,
       and_10_out, and_11_out, and_12_out, and_13_out, and_14_out, and_15_out, and_16_out, and_17_out,
       and_18_out, and_19_out, and_20_out, and_21_out, and_22_out, and_23_out, and_24_out, and_25_out,
       and_26_out, and_27_out, and_28_out, and_29_out, and_30_out, and_31_out, and_32_out, and_33_out,
       and_34_out, and_35_out, and_36_out, and_37_out, and_38_out, and_39_out, and_40_out, and_41_out,
       and_42_out, and_43_out, and_44_out, and_45_out, and_46_out, and_47_out, and_48_out, and_49_out,
       and_50_out, or_1_out, or_2_out, or_3_out, or_4_out, or_5_out, or_6_out, or_7_out, xor_1_out,
       xor_2_out, xor_3_out, xor_4_out, xor_5_out, xor_6_out, xor_7_out, xor_8_out, xor_9_out, xor_10_out,
       xor_11_out, xor_12_out, xor_13_out, xor_14_out;

  and and_1 (and_1_out, in_6, in_12);
  and and_2 (and_2_out, in_6, in_11);
  and and_3 (and_3_out, in_6, in_10);
  and and_4 (and_4_out, in_6, in_9);
  and and_5 (and_5_out, in_6, in_8);
  and and_6 (and_6_out, in_6, in_7);
  and and_7 (and_7_out, in_5, in_12);
  and and_8 (and_8_out, in_5, in_11);
  and and_9 (and_9_out, in_5, in_10);
  and and_10 (and_10_out, in_5, in_9);
  and and_11 (and_11_out, in_5, in_8);
  and and_12 (and_12_out, in_5, in_7);
  and and_13 (and_13_out, in_4, in_12);
  and and_14 (and_14_out, in_4, in_11);
  and and_15 (and_15_out, in_4, in_10);
  and and_16 (and_16_out, in_4, in_9);
  and and_17 (and_17_out, in_4, in_8);
  and and_18 (and_18_out, in_4, in_7);
  and and_19 (and_19_out, in_3, in_12);
  and and_20 (and_20_out, in_3, in_11);
  and and_21 (and_21_out, in_3, in_10);
  and and_22 (and_22_out, in_3, in_9);
  and and_23 (and_23_out, in_3, in_8);
  and and_24 (and_24_out, in_3, in_7);
  and and_25 (and_25_out, in_2, in_12);
  and and_26 (and_26_out, in_2, in_11);
  and and_27 (and_27_out, in_2, in_10);
  and and_28 (and_28_out, in_2, in_9);
  and and_29 (and_29_out, in_2, in_8);
  and and_30 (and_30_out, in_2, in_7);
  and and_31 (and_31_out, in_1, in_12);
  and and_32 (and_32_out, in_1, in_11);
  and and_33 (and_33_out, in_1, in_10);
  and and_34 (and_34_out, in_1, in_9);
  and and_35 (and_35_out, in_1, in_8);
  and and_36 (and_36_out, in_1, in_7);
  LED led_1 (.in(or_7_out));
  LED led_2 (.in(xor_14_out));
  LED led_3 (.in(xor_11_out));
  LED led_4 (.in(xor_12_out));
  LED led_5 (.in(xor_13_out));
  LED led_6 (.in(xor_9_out));
  LED led_7 (.in(xor_10_out));
  LED led_8 (.in(xor_8_out));
  xor xor_1 (xor_1_out, and_1_out, 1'b0);
  and and_37 (and_37_out, and_1_out, 1'b0);
  xor xor_2 (xor_2_out, and_7_out, and_2_out);
  and and_38 (and_38_out, and_7_out, and_2_out);
  xor xor_3 (xor_3_out, and_13_out, and_8_out);
  and and_39 (and_39_out, and_13_out, and_8_out);
  xor xor_4 (xor_4_out, and_19_out, and_14_out);
  and and_40 (and_40_out, and_19_out, and_14_out);
  xor xor_5 (xor_5_out, and_25_out, and_20_out);
  and and_41 (and_41_out, and_25_out, and_20_out);
  xor xor_6 (xor_6_out, and_31_out, and_26_out);
  and and_42 (and_42_out, and_31_out, and_26_out);
  xor xor_7 (xor_7_out, 1'b0, and_32_out);
  and and_43 (and_43_out, 1'b0, and_32_out);
  xor xor_8 (xor_8_out, in_13, xor_1_out);
  and and_44 (and_44_out, in_13, xor_1_out);
  xor xor_9 (xor_9_out, or_1_out, xor_2_out);
  and and_45 (and_45_out, or_1_out, xor_2_out);
  xor xor_10 (xor_10_out, or_2_out, xor_3_out);
  and and_46 (and_46_out, or_2_out, xor_3_out);
  xor xor_11 (xor_11_out, or_3_out, xor_4_out);
  and and_47 (and_47_out, or_3_out, xor_4_out);
  xor xor_12 (xor_12_out, or_4_out, xor_5_out);
  and and_48 (and_48_out, or_4_out, xor_5_out);
  xor xor_13 (xor_13_out, or_5_out, xor_6_out);
  and and_49 (and_49_out, or_5_out, xor_6_out);
  xor xor_14 (xor_14_out, or_6_out, xor_7_out);
  and and_50 (and_50_out, or_6_out, xor_7_out);
  or or_1 (or_1_out, and_44_out, and_37_out);
  or or_2 (or_2_out, and_45_out, and_38_out);
  or or_3 (or_3_out, and_46_out, and_39_out);
  or or_4 (or_4_out, and_47_out, and_40_out);
  or or_5 (or_5_out, and_48_out, and_41_out);
  or or_6 (or_6_out, and_49_out, and_42_out);
  or or_7 (or_7_out, and_50_out, and_43_out);
endmodule
