// Logisim project ram value transfer.circ as structural Verilog: 1 circuit, main circuit main
module main (
  input  [5:0] in_1,
  input  [5:0] in_2,
  input  [5:0] in_3,
  input  [5:0] in_4,
  input  [5:0] in_5,
  input  [5:0] in_6,
  output [5:0] out_7,
  output [5:0] out_8,
  output [5:0] out_9
);

  wire and_1_out, and_2_out, and_3_out, and_4_out, and_5_out, and_6_out, and_7_out, and_8_out, and_9_out,
       and_10_out, and_11_out, and_12_out, and_13_out, and_14_out, and_15_out, and_16_out, and_17_out,
       and_18_out, and_19_out, and_20_out, and_21_out, and_22_out, and_23_out, and_24_out, and_25_out,
       and_26_out, and_27_out, and_28_out, and_29_out, and_30_out, not_1_out, not_2_out, not_3_out;

  not not_1 (not_1_out, in_1[2]);
  not not_2 (not_2_out, in_3[2]);
  not not_3 (not_3_out, in_5[2]);
  and and_1 (and_1_out, in_1[1], not_1_out);
  and and_2 (and_2_out, in_1[3], in_1[4]);
  and and_3 (and_3_out, in_2[0], in_2[1]);
  and and_4 (and_4_out, in_2[2], in_2[3]);
  and and_5 (and_5_out, in_2[4], in_2[5]);
  and and_6 (and_6_out, in_3[1], not_2_out);
  and and_7 (and_7_out, in_3[3], in_3[4]);
  and and_8 (and_8_out, in_4[0], in_4[1]);
  and and_9 (and_9_out, in_4[2], in_4[3]);
  and and_10 (and_10_out, in_4[4], in_4[5]);
  and and_11 (and_11_out, in_5[1], not_3_out);
  and and_12 (and_12_out, in_5[3], in_5[4]);
  and and_13 (and_13_out, in_6[0], in_6[1]);
  and and_14 (and_14_out, in_6[2], in_6[3]);
  and and_15 (and_15_out, in_6[4], in_6[5]);
  and and_16 (and_16_out, and_1_out, and_2_out);
  and and_17 (and_17_out, and_16_out, in_1[5]);
  and and_18 (and_18_out, and_3_out, and_4_out);
  and and_19 (and_19_out, and_18_out, and_5_out);
  and and_20 (and_20_out, and_6_out, and_7_out);
  and and_21 (and_21_out, and_20_out, in_3[5]);
  and and_22 (and_22_out, and_8_out, and_9_out);
  and and_23 (and_23_out, and_22_out, and_10_out);
  and and_24 (and_24_out, and_11_out, and_12_out);
  and and_25 (and_25_out, and_24_out, in_5[5]);
  and and_26 (and_26_out, and_13_out, and_14_out);
  and and_27 (and_27_out, and_26_out, and_15_out);
  and and_28 (and_28_out, and_17_out, and_19_out);
  and and_29 (and_29_out, and_21_out, and_23_out);
  and and_30 (and_30_out, and_25_out, and_27_out);
  and and_31 (out_7[5], in_4[5], and_28_out);
  and and_32 (out_8[5], in_6[5], and_29_out);
  and and_33 (out_9[5], in_2[5], and_30_out);
  and and_34 (out_7[4], in_4[4], and_28_out);
  and and_35 (out_8[4], in_6[4], and_29_out);
  and and_36 (out_9[4], in_2[4], and_30_out);
  and and_37 (out_7[3], in_4[3], and_28_out);
  and and_38 (out_8[3], in_6[3], and_29_out);
  and and_39 (out_9[3], in_2[3], and_30_out);
  and and_40 (out_7[2], in_4[2], and_28_out);
  and and_41 (out_8[2], in_6[2], and_29_out);
  and and_42 (out_9[2], in_2[2], and_30_out);
  and and_43 (out_7[1], in_4[1], and_28_out);
  and and_44 (out_8[1], in_6[1], and_29_out);
  and and_45 (out_9[1], in_2[1], and_30_out);
  and and_46 (out_7[0], in_4[0], and_28_out);
  and and_47 (out_8[0], in_6[0], and_29_out);
  and and_48 (out_9[0], in_2[0], and_30_out);
endmodule
