// Logisim project subtraction using 2s compliment.circ as structural Verilog: 1 circuit, main circuit main
module main (
  input  in_1,
  input  in_2,
  input  in_3,
  input  in_4,
  input  in_5,
  input  in_6,
  input  in_7,
  input  in_8,
  input  in_9,
  input  in_10,
  input  in_11,
  input  in_12,
  output out_13,
  output out_14,
  output out_15,
  output out_16,
  output out_17,
  output out_18
);

  wire and_1_out, and_2_out, and_3_out, and_4_out, and_5_out, and_6_out, main_1_out_13, not_1_out, not_2_out,
       not_3_out, not_4_out, not_5_out, not_6_out, xor_1_out, xor_2_out, xor_3_out, xor_4_out, xor_5_out,
       xor_6_out;

  LED led_1 (.in(main_1_out_13));
  addition_main main_1 (
    .in_1(in_1), .in_2(in_2), .in_3(in_3), .in_4(in_4), .in_5(in_5), .in_6(in_6), .in_7(xor_6_out),
    .in_8(xor_5_out), .in_9(xor_4_out), .in_10(xor_3_out), .in_11(xor_2_out), .in_12(xor_1_out),
    .out_13(main_1_out_13), .out_14(out_13), .out_15(out_14), .out_16(out_15), .out_17(out_16),
    .out_18(out_17), .out_19(out_18));
  LED led_2 (.in(and_6_out));
  not not_1 (not_1_out, in_7);
  not not_2 (not_2_out, in_10);
  not not_3 (not_3_out, in_9);
  not not_4 (not_4_out, in_8);
  not not_5 (not_5_out, in_12);
  not not_6 (not_6_out, in_11);
  xor xor_1 (xor_1_out, 1'b1, not_5_out);
  and and_1 (and_1_out, 1'b1, not_5_out);
  xor xor_2 (xor_2_out, and_1_out, not_6_out);
  and and_2 (and_2_out, and_1_out, not_6_out);
  xor xor_3 (xor_3_out, and_2_out, not_2_out);
  and and_3 (and_3_out, and_2_out, not_2_out);
  xor xor_4 (xor_4_out, and_3_out, not_3_out);
  and and_4 (and_4_out, and_3_out, not_3_out);
  xor xor_5 (xor_5_out, and_4_out, not_4_out);
  and and_5 (and_5_out, and_4_out, not_4_out);
  xor xor_6 (xor_6_out, and_5_out, not_1_out);
  and and_6 (and_6_out, and_5_out, not_1_out);
endmodule
